// Logisim project CRC校验(P0.Q1).circ as structural Verilog: 2 circuits, main circuit CRC
module CRC (
  input  [7:0] A,
  input  [3:0] B,
  output [10:0] C
);

  wire [2:0] \四位模二除法器_1_c , \四位模二除法器_2_c , \四位模二除法器_3_c , \四位模二除法器_4_c , \四位模二除法器_5_c , \四位模二除法器_6_c ,
       \四位模二除法器_7_c ;

  \四位模二除法器  \u_四位模二除法器_1  (.A(A[7:4]), .B(B), .C(\四位模二除法器_1_c ));  // open: D
  \四位模二除法器  \u_四位模二除法器_2  (.A({\四位模二除法器_1_c , A[3]}), .B(B), .C(\四位模二除法器_2_c ));  // open: D
  \四位模二除法器  \u_四位模二除法器_3  (.A({\四位模二除法器_2_c , A[2]}), .B(B), .C(\四位模二除法器_3_c ));  // open: D
  \四位模二除法器  \u_四位模二除法器_4  (.A({\四位模二除法器_3_c , A[1]}), .B(B), .C(\四位模二除法器_4_c ));  // open: D
  \四位模二除法器  \u_四位模二除法器_5  (.A({\四位模二除法器_4_c , A[0]}), .B(B), .C(\四位模二除法器_5_c ));  // open: D
  \四位模二除法器  \u_四位模二除法器_6  (.A({\四位模二除法器_5_c , 1'b0}), .B(B), .C(\四位模二除法器_6_c ));  // open: D
  \四位模二除法器  \u_四位模二除法器_7  (.A({\四位模二除法器_6_c , 1'b0}), .B(B), .C(\四位模二除法器_7_c ));  // open: D
  \四位模二除法器  \u_四位模二除法器_8  (.A({\四位模二除法器_7_c , 1'b0}), .B(B), .C(C[2:0]));  // open: D

  assign C[10:3] = A;

  // Other names for the same wires on the sheet: 被除数[7:0] = A; 除数[3:0] = B
endmodule

module \四位模二除法器  (
  input  [3:0] A,
  input  [3:0] B,
  output [2:0] C,
  output D
);

  wire [3:0] xor_1_out;
  wire [3:3] multiplexer_1_out;

  assign xor_1_out = A ^ B;  // XOR_Gate xor_1, 4 bits wide
  Multiplexer #(.width(4)) multiplexer_1 (
    .in0(A), .in1(xor_1_out), .out({multiplexer_1_out[3], C}), .sel(A[3]));  // open: en

  assign D = A[3];
endmodule
