// Logisim project Logisim中的FSM(P0.Q4)正则表达式匹配.circ as structural Verilog: 3 circuits, main circuit fsm
module fsm (
  input  [1:0] in,
  input  clr,
  output z
);

  wire clk, multiplexer_1_out, multiplexer_2_out, s0_, s1_, \状态转移_1_s0_ , \状态转移_1_s1_ ;

  Clock clock_1 (.out(clk));
  \状态转移  \u_状态转移_1  (.s1(s1_), .s0(s0_), .in1(in[1]), .in0(in[0]), .s1_(\状态转移_1_s1_ ), .s0_(\状态转移_1_s0_ ));
  \输出  \u_输出_1  (.s1(s1_), .s0(s0_), .in1(in[1]), .in0(in[0]), .z(z));
  Multiplexer multiplexer_1 (.in0(\状态转移_1_s1_ ), .in1(1'b0), .out(multiplexer_1_out), .sel(clr));  // open: en
  Multiplexer multiplexer_2 (.in0(\状态转移_1_s0_ ), .in1(1'b0), .out(multiplexer_2_out), .sel(clr));  // open: en
  Register #(.width(1)) register_1 (.D(multiplexer_1_out), .Q(s1_), .clk(clk));  // open: en, clr
  Register #(.width(1)) register_2 (.D(multiplexer_2_out), .Q(s0_), .clk(clk));  // open: en, clr

  // Notes on the sheet:
  //   同步复位
endmodule

module \状态转移  (
  input  s1,
  input  s0,
  input  in1,
  input  in0,
  output s1_,
  output s0_
);

  wire not_1_out, not_2_out;

  and and_1 (s1_, s0, not_1_out);
  not not_1 (not_1_out, in0);
  not not_2 (not_2_out, in1);
  and and_2 (s0_, not_2_out, in0);
endmodule

module \输出  (
  input  s1,
  input  s0,
  input  in1,
  input  in0,
  output z
);

  wire not_1_out, not_2_out;

  and and_1 (z, s1, not_1_out, not_2_out);
  not not_1 (not_1_out, s0);
  not not_2 (not_2_out, in0);
endmodule
