// Logisim project Logisim导航(P0.Q3) .circ as structural Verilog: 4 circuits, main circuit navigation
module navigation (
  input  [1:0] dir,
  input  in_2,
  input  in_3,
  output out_4,
  output out_5
);

  wire s0_, s1_, s2_, \转移_1_s0_ , \转移_1_s1_ , \转移_1_s2_ , \输出hit_1_hit ;

  \转移  \u_转移_1  (
    .s2(s2_), .s1(s1_), .s0(s0_), .dir1(dir[1]), .dir0(dir[0]), .s2_(\转移_1_s2_ ), .s1_(\转移_1_s1_ ),
    .s0_(\转移_1_s0_ ));
  Register #(.width(1)) register_1 (.D(\转移_1_s2_ ), .Q(s2_), .clk(in_2), .clr(in_3));  // open: en
  Register #(.width(1)) register_2 (.D(\转移_1_s1_ ), .Q(s1_), .clk(in_2), .clr(in_3));  // open: en
  Register #(.width(1)) register_3 (.D(\转移_1_s0_ ), .Q(s0_), .clk(in_2), .clr(in_3));  // open: en
  \输出hit  \u_输出hit_1  (.s2(s2_), .s1(s1_), .s0(s0_), .dir1(dir[1]), .dir0(dir[0]), .hit(\输出hit_1_hit ));
  \输出arrive_moore  \u_输出arrive_moore_1  (.s2(s2_), .s1(s1_), .s0(s0_), .arrive(out_4));
  // Probe on out_5
  // Probe on \输出hit_1_hit 
  Register #(.width(1)) register_4 (.D(\输出hit_1_hit ), .Q(out_5), .clk(in_2), .clr(in_3));  // open: en

  // Other names for the same wires on the sheet: arrive = out_4; clk = in_2; hit = out_5; reset = in_3

  // Notes on the sheet:
  //   此处arrive采用第二种方式
  //   此题重点在于hit的输出时机不是dir变则立即改变，这是mealy的行为
  //   而本题要求hit需要在时钟上升沿改变，所以需要加入一个寄存器
  //   注意，若arrive的真值表用的是现态和dir作为输入，则需要寄存器；
  //   若是次态作为输入，则不需要寄存器
endmodule

module \输出arrive_moore  (
  input  s2,
  input  s1,
  input  s0,
  output arrive
);


  assign arrive = s2;
endmodule

module \输出hit  (
  input  s2,
  input  s1,
  input  s0,
  input  dir1,
  input  dir0,
  output hit
);

  wire and_1_out, and_2_out, and_3_out, and_4_out, and_5_out, not_1_out, not_2_out, not_3_out, not_4_out,
       not_5_out, not_6_out, not_7_out, not_8_out, not_9_out, not_10_out, not_11_out;

  not not_1 (not_1_out, s2);
  not not_2 (not_2_out, s0);
  not not_3 (not_3_out, dir1);
  not not_4 (not_4_out, s2);
  not not_5 (not_5_out, s1);
  not not_6 (not_6_out, s0);
  not not_7 (not_7_out, s2);
  not not_8 (not_8_out, s0);
  not not_9 (not_9_out, dir0);
  not not_10 (not_10_out, dir1);
  not not_11 (not_11_out, dir0);
  and and_1 (and_1_out, not_1_out, not_2_out, not_3_out, dir0);
  and and_2 (and_2_out, not_4_out, not_5_out, not_6_out, dir1);
  and and_3 (and_3_out, not_7_out, not_8_out, dir1, not_9_out);
  and and_4 (and_4_out, s0, dir1, dir0);
  and and_5 (and_5_out, s1, s0, not_10_out, not_11_out);
  or or_1 (hit, and_1_out, and_2_out, and_3_out, and_4_out, and_5_out);
endmodule

module \转移  (
  input  s2,
  input  s1,
  input  s0,
  input  dir1,
  input  dir0,
  output s2_,
  output s1_,
  output s0_
);

  wire and_1_out, and_2_out, and_3_out, and_4_out, and_5_out, and_6_out, and_7_out, and_8_out, and_9_out,
       and_10_out, and_11_out, not_1_out, not_2_out, not_3_out, not_4_out, not_5_out, not_6_out, not_7_out,
       not_8_out, not_9_out, not_10_out, not_11_out, not_12_out, not_13_out, not_14_out, not_15_out,
       not_16_out, not_17_out;

  not not_1 (not_1_out, s0);
  not not_2 (not_2_out, dir1);
  not not_3 (not_3_out, dir0);
  not not_4 (not_4_out, dir1);
  not not_5 (not_5_out, s1);
  not not_6 (not_6_out, dir1);
  not not_7 (not_7_out, dir1);
  not not_8 (not_8_out, dir0);
  not not_9 (not_9_out, s0);
  not not_10 (not_10_out, dir1);
  not not_11 (not_11_out, s0);
  not not_12 (not_12_out, dir0);
  not not_13 (not_13_out, s2);
  not not_14 (not_14_out, s1);
  not not_15 (not_15_out, dir1);
  not not_16 (not_16_out, dir0);
  not not_17 (not_17_out, dir0);
  and and_1 (and_1_out, s1, not_1_out, not_2_out, not_3_out);
  and and_2 (and_2_out, s1, s0, not_4_out, dir0);
  and and_3 (and_3_out, not_5_out, s0, not_6_out);
  and and_4 (and_4_out, s0, not_7_out, not_8_out);
  and and_5 (and_5_out, s1, not_9_out, not_10_out, dir0);
  and and_6 (and_6_out, s1, not_11_out, dir1, not_12_out);
  and and_7 (and_7_out, s1, s0, dir1, dir0);
  and and_8 (and_8_out, not_13_out, not_14_out, not_15_out, not_16_out);
  and and_9 (and_9_out, s0, dir1, dir0);
  and and_10 (and_10_out, s1, dir1, dir0);
  and and_11 (and_11_out, s1, s0, not_17_out);
  or or_1 (s2_, and_1_out, and_2_out);
  or or_2 (s1_, and_3_out, and_4_out, and_5_out, and_6_out, and_7_out);
  or or_3 (s0_, and_8_out, and_9_out, and_10_out, and_11_out);
endmodule
