// Logisim project P0_L1_ftoi(P0.附加题).circ as structural Verilog: 3 circuits, main circuit ftoi
module ftoi (
  input  [15:0] float,
  output [31:0] \int 
);

  wire \类型判断_1_sel ;
  wire [4:0] E;
  wire [31:0] negator_1_out, res, \计算_1_out_3 ;

  \计算  \u_计算_1  (.fraction(float[9:0]), .E(E), .out_3(\计算_1_out_3 ));
  // Probe on \int 
  Negator #(.width(32)) negator_1 (.in(\计算_1_out_3 ), .out(negator_1_out));
  Multiplexer #(.width(32)) multiplexer_1 (
    .in0(\计算_1_out_3 ), .in1(negator_1_out), .out(res), .sel(float[15]));  // open: en
  // Probe on E
  Subtractor #(.width(5)) subtractor_1 (.a(float[14:10]), .b(5'b01111), .out(E));  // open: bin, bout
  \类型判断  \u_类型判断_1  (.sel(\类型判断_1_sel ), .ex(float[14:10]));
  Multiplexer #(.width(32)) multiplexer_2 (.in0({32{1'b0}}), .in1(res), .out(\int ), .sel(\类型判断_1_sel ));  // open: en

  // Other names for the same wires on the sheet: fraction[9:0] = float[9:0]; exponent[4:0] = float[14:10];
  //   sign = float[15]
endmodule

module \类型判断  (
  input  [4:0] ex,
  output sel
);

  wire and_1_out, and_2_out, and_3_out, and_4_out, and_5_out, and_6_out, and_7_out, and_8_out, not_1_out,
       not_2_out, not_3_out, not_4_out, not_5_out, not_6_out, not_7_out, not_8_out;

  not not_1 (not_1_out, ex[4]);
  and and_1 (and_1_out, not_1_out, ex[0]);
  not not_2 (not_2_out, ex[4]);
  and and_2 (and_2_out, not_2_out, ex[1]);
  not not_3 (not_3_out, ex[4]);
  and and_3 (and_3_out, not_3_out, ex[2]);
  not not_4 (not_4_out, ex[4]);
  and and_4 (and_4_out, not_4_out, ex[3]);
  and and_5 (and_5_out, ex[4], not_5_out);
  not not_5 (not_5_out, ex[3]);
  and and_6 (and_6_out, ex[4], not_6_out);
  not not_6 (not_6_out, ex[2]);
  and and_7 (and_7_out, ex[4], not_7_out);
  not not_7 (not_7_out, ex[1]);
  and and_8 (and_8_out, ex[4], not_8_out);
  not not_8 (not_8_out, ex[0]);
  or or_1 (sel, and_1_out, and_2_out, and_3_out, and_4_out, and_5_out, and_6_out, and_7_out, and_8_out);

  // Notes on the sheet:
  //   ex=00000或11111时，sel为0；其余为1
endmodule

module \计算  (
  input  [9:0] fraction,
  input  [4:0] E,
  output [31:0] out_3
);

  wire comparator_1_lt;
  wire [9:0] shifter_1_out;
  wire [21:0] \移位结果 ;

  Shifter #(.width(32)) shifter_1 (.in({22'h1, fraction}), .\dist (E), .out({\移位结果 , shifter_1_out}));
  Multiplexer #(.width(32)) multiplexer_1 (
    .in0({{10{1'b0}}, \移位结果 }), .in1({32{1'b0}}), .out(out_3), .sel(comparator_1_lt));  // open: en
  Comparator #(.width(5)) comparator_1 (.a(E), .b({5{1'b0}}), .lt(comparator_1_lt));  // open: gt, eq

  // Other names for the same wires on the sheet: 计算结果[31:0] = out_3

  // Notes on the sheet:
  //   这里的移位是核心算法
endmodule
