// Logisim project dmx三态作用演示.circ as structural Verilog: 1 circuit, main circuit main
module main (
  input  in_1,
  input  in_2,
  input  in_3
);

  wire demultiplexer_1_out0, demultiplexer_1_out1, demultiplexer_2_out0, demultiplexer_2_out1;

  Demultiplexer demultiplexer_1 (
    .out0(demultiplexer_1_out0), .out1(demultiplexer_1_out1), .in(in_2), .sel(in_3));  // open: en
  Register #(.width(1)) register_1 (.D(demultiplexer_1_out0), .clk(in_1));  // open: en, Q, clr
  Register #(.width(1)) register_2 (.D(demultiplexer_1_out1), .clk(in_1));  // open: en, Q, clr
  Demultiplexer #(.tristate("true")) demultiplexer_2 (
    .out0(demultiplexer_2_out0), .out1(demultiplexer_2_out1), .in(in_2), .sel(in_3));  // open: en
  Register #(.width(1)) register_3 (.D(demultiplexer_2_out0), .clk(in_1));  // open: en, Q, clr
  Register #(.width(1)) register_4 (.D(demultiplexer_2_out1), .clk(in_1));  // open: en, Q, clr

  // Other names for the same wires on the sheet: clk = in_1; in = in_2; sel = in_3

  // Notes on the sheet:
  //   三态关
  //   演示步骤：1.sel置0，in置1，双击clk
  //   2.sel置1，in置1，双击clk
  //   三态开
  //   结论：会发现三态开的话，未选择的输出端线路为蓝色，代表浮空值x，对应寄存器的值在时钟上升沿不变
  //   三态关的话，未选择的输出端线路为深绿色，代表0，对应寄存器的值在时钟上升沿清零
endmodule
