// Logisim project cpu V2.2.circ as structural Verilog: 11 circuits, main circuit main
module main (
  input  Reset,
  output [31:0] Instr,
  output RegWrite,
  output [4:0] RegAddr,
  output [31:0] RegData,
  output MemWrite,
  output [4:0] MemAddr,
  output [31:0] MemData
);

  wire clk, Zero;
  wire [2:0] ALUSrcSel, EXTOp, LSel, NPCOp, RegDstSel, SSel, toRegSel;
  wire [3:0] ALUOp;
  wire [4:0] shamt, splitter_1_rd_15_11, splitter_1_rs_25_21, splitter_1_rt_20_16;
  wire [5:0] splitter_1_func_5_0, splitter_1_op_31_26;
  wire [15:0] splitter_1_imm_15_0;
  wire [25:0] splitter_1_imm26_25_0;
  wire [31:0] dm2_1_rd, ext_1_o, grf_1_rd1, MemAddr32, multiplexer_2_out, npc_1_npc, npc_1_pc4, pc_1_pc;

  // Probe on npc_1_npc
  // Probe on NPCOp
  // Probe on pc_1_pc
  PC pc_1 (.NPC(npc_1_npc), .PC(pc_1_pc), .clk(clk), .reset(Reset));
  NPC npc_1 (
    .Zero(Zero), .NPC(npc_1_npc), .PC4(npc_1_pc4), .NPCOp(NPCOp), .RA(grf_1_rd1), .PC(pc_1_pc),
    .Imm26(splitter_1_imm26_25_0));
  Clock clock_1 (.out(clk));
  // Probe on Instr
  IM im_1 (.A(pc_1_pc), .RD(Instr));
  SPLITTER splitter_1 (
    .I(Instr), .Imm_15_0(splitter_1_imm_15_0), .Rd_15_11(splitter_1_rd_15_11),
    .Rt_20_16(splitter_1_rt_20_16), .Rs_25_21(splitter_1_rs_25_21), .Op_31_26(splitter_1_op_31_26),
    .Imm26_25_0(splitter_1_imm26_25_0), .Func_5_0(splitter_1_func_5_0), .Shamt_10_6(shamt));
  Multiplexer #(.select(3), .width(5)) multiplexer_1 (
    .in0(splitter_1_rt_20_16), .in1(splitter_1_rd_15_11), .in2({5{1'b1}}), .out(RegAddr), .sel(RegDstSel));  // open: in3, in4, in5, in6, in7, en
  Control control_1 (
    .Op(splitter_1_op_31_26), .Func(splitter_1_func_5_0), .RegDstSel(RegDstSel), .ALUSrcSel(ALUSrcSel),
    .toRegSel(toRegSel), .RegWrite(RegWrite), .MemWrite(MemWrite), .NPCOp(NPCOp), .ALUOp(ALUOp),
    .ExtOp(EXTOp), .SSel(SSel), .LSel(LSel));
  GRF grf_1 (
    .clk(clk), .reset(Reset), .WE(RegWrite), .A1(splitter_1_rs_25_21), .A2(splitter_1_rt_20_16),
    .WD(RegData), .A3(RegAddr), .RD1(grf_1_rd1), .RD2(MemData));
  EXT ext_1 (.I(splitter_1_imm_15_0), .EXTop(EXTOp), .O(ext_1_o));
  Multiplexer #(.select(3), .width(32)) multiplexer_2 (
    .in0(MemData), .in1(ext_1_o), .out(multiplexer_2_out), .sel(ALUSrcSel));  // open: in2, in3, in4, in5, in6, in7, en
  ALU alu_1 (
    .A(grf_1_rd1), .B(multiplexer_2_out), .ALUOp(ALUOp), .Zero(Zero),
    .Result({MemAddr32[31:7], MemAddr, MemAddr32[1:0]}), .shamt(shamt));
  DM2 dm2_1 (
    .A({MemAddr32[31:7], MemAddr, MemAddr32[1:0]}), .WD(MemData), .WE(MemWrite), .clk(clk), .reset(Reset),
    .RD(dm2_1_rd), .SSel(SSel), .LSel(LSel));
  Multiplexer #(.select(3), .width(32)) multiplexer_3 (
    .in0({MemAddr32[31:7], MemAddr, MemAddr32[1:0]}), .in1(dm2_1_rd), .in2(ext_1_o), .in3(npc_1_pc4),
    .out(RegData), .sel(toRegSel));  // open: in4, in5, in6, in7, en

  // Other names for the same wires on the sheet: MemAddr32[6:2] = MemAddr; MemW = MemWrite; RegW = RegWrite;
  //   rst = Reset
endmodule

module GRF (
  input  clk,
  input  reset,
  input  WE,
  input  [4:0] A1,
  input  [4:0] A2,
  input  [31:0] WD,
  input  [4:0] A3,
  output [31:0] RD1,
  output [31:0] RD2
);

  wire [31:0] in1, in2, in3, in4, in5, in6, in7, in8, in9, in10, in11, in12, in13, in14, in15, in16, in17,
       in18, in19, in20, in21, in22, in23, in24, in25, in26, in27, in28, in29, in30, in31, out0, out1, out2,
       out3, out4, out5, out6, out7, out8, out9, out10, out11, out12, out13, out14, out15, out16, out17,
       out18, out19, out20, out21, out22, out23, out24, out25, out26, out27, out28, out29, out30, out31;

  Register #(.width(32)) _0 (.D({32{1'b0}}), .en(WE), .Q(out0), .clk(clk), .clr(reset));
  Register #(.width(32)) _1 (.D(in1), .en(WE), .Q(out1), .clk(clk), .clr(reset));
  Register #(.width(32)) _2 (.D(in2), .en(WE), .Q(out2), .clk(clk), .clr(reset));
  Register #(.width(32)) _3 (.D(in3), .en(WE), .Q(out3), .clk(clk), .clr(reset));
  Register #(.width(32)) _4 (.D(in4), .en(WE), .Q(out4), .clk(clk), .clr(reset));
  Register #(.width(32)) _5 (.D(in5), .en(WE), .Q(out5), .clk(clk), .clr(reset));
  Register #(.width(32)) _6 (.D(in6), .en(WE), .Q(out6), .clk(clk), .clr(reset));
  Register #(.width(32)) _7 (.D(in7), .en(WE), .Q(out7), .clk(clk), .clr(reset));
  Register #(.width(32)) _8 (.D(in8), .en(WE), .Q(out8), .clk(clk), .clr(reset));
  Register #(.width(32)) _9 (.D(in9), .en(WE), .Q(out9), .clk(clk), .clr(reset));
  Register #(.width(32)) _10 (.D(in10), .en(WE), .Q(out10), .clk(clk), .clr(reset));
  Register #(.width(32)) _11 (.D(in11), .en(WE), .Q(out11), .clk(clk), .clr(reset));
  Register #(.width(32)) _12 (.D(in12), .en(WE), .Q(out12), .clk(clk), .clr(reset));
  Register #(.width(32)) _13 (.D(in13), .en(WE), .Q(out13), .clk(clk), .clr(reset));
  Register #(.width(32)) _14 (.D(in14), .en(WE), .Q(out14), .clk(clk), .clr(reset));
  Register #(.width(32)) _15 (.D(in15), .en(WE), .Q(out15), .clk(clk), .clr(reset));
  Register #(.width(32)) _16 (.D(in16), .en(WE), .Q(out16), .clk(clk), .clr(reset));
  Register #(.width(32)) _17 (.D(in17), .en(WE), .Q(out17), .clk(clk), .clr(reset));
  Register #(.width(32)) _18 (.D(in18), .en(WE), .Q(out18), .clk(clk), .clr(reset));
  Register #(.width(32)) _19 (.D(in19), .en(WE), .Q(out19), .clk(clk), .clr(reset));
  Register #(.width(32)) _20 (.D(in20), .en(WE), .Q(out20), .clk(clk), .clr(reset));
  Register #(.width(32)) _21 (.D(in21), .en(WE), .Q(out21), .clk(clk), .clr(reset));
  Register #(.width(32)) _22 (.D(in22), .en(WE), .Q(out22), .clk(clk), .clr(reset));
  Register #(.width(32)) _23 (.D(in23), .en(WE), .Q(out23), .clk(clk), .clr(reset));
  Register #(.width(32)) _24 (.D(in24), .en(WE), .Q(out24), .clk(clk), .clr(reset));
  Register #(.width(32)) _25 (.D(in25), .en(WE), .Q(out25), .clk(clk), .clr(reset));
  Register #(.width(32)) _26 (.D(in26), .en(WE), .Q(out26), .clk(clk), .clr(reset));
  Register #(.width(32)) _27 (.D(in27), .en(WE), .Q(out27), .clk(clk), .clr(reset));
  Register #(.width(32)) _28 (.D(in28), .en(WE), .Q(out28), .clk(clk), .clr(reset));
  Register #(.width(32)) _29 (.D(in29), .en(WE), .Q(out29), .clk(clk), .clr(reset));
  Register #(.width(32)) _30 (.D(in30), .en(WE), .Q(out30), .clk(clk), .clr(reset));
  Register #(.width(32)) _31 (.D(in31), .en(WE), .Q(out31), .clk(clk), .clr(reset));
  Multiplexer #(.select(5), .width(32)) multiplexer_1 (
    .in0(out0), .in1(out1), .in2(out2), .in3(out3), .in4(out4), .in5(out5), .in6(out6), .in7(out7),
    .in8(out8), .in9(out9), .in10(out10), .in11(out11), .in12(out12), .in13(out13), .in14(out14),
    .in15(out15), .in16(out16), .in17(out17), .in18(out18), .in19(out19), .in20(out20), .in21(out21),
    .in22(out22), .in23(out23), .in24(out24), .in25(out25), .in26(out26), .in27(out27), .in28(out28),
    .in29(out29), .in30(out30), .in31(out31), .out(RD1), .sel(A1));  // open: en
  Demultiplexer #(.select(5), .width(32), .tristate("true")) demultiplexer_1 (
    .out1(in1), .out2(in2), .out3(in3), .out4(in4), .out5(in5), .out6(in6), .out7(in7), .out8(in8),
    .out9(in9), .out10(in10), .out11(in11), .out12(in12), .out13(in13), .out14(in14), .out15(in15),
    .out16(in16), .out17(in17), .out18(in18), .out19(in19), .out20(in20), .out21(in21), .out22(in22),
    .out23(in23), .out24(in24), .out25(in25), .out26(in26), .out27(in27), .out28(in28), .out29(in29),
    .out30(in30), .out31(in31), .in(WD), .sel(A3));  // open: out0, en
  Multiplexer #(.select(5), .width(32)) multiplexer_2 (
    .in0(out0), .in1(out1), .in2(out2), .in3(out3), .in4(out4), .in5(out5), .in6(out6), .in7(out7),
    .in8(out8), .in9(out9), .in10(out10), .in11(out11), .in12(out12), .in13(out13), .in14(out14),
    .in15(out15), .in16(out16), .in17(out17), .in18(out18), .in19(out19), .in20(out20), .in21(out21),
    .in22(out22), .in23(out23), .in24(out24), .in25(out25), .in26(out26), .in27(out27), .in28(out28),
    .in29(out29), .in30(out30), .in31(out31), .out(RD2), .sel(A2));  // open: en
endmodule

module PC (
  input  [31:0] NPC,
  input  clk,
  input  reset,
  output [31:0] PC
);

  wire comparator_1_eq;
  wire [31:0] \程序计数器_q ;

  Register #(.width(32)) \u_程序计数器  (.D(NPC), .Q(\程序计数器_q ), .clk(clk), .clr(reset));  // open: en
  Comparator #(.width(32)) comparator_1 (.a(\程序计数器_q ), .b({32{1'b0}}), .eq(comparator_1_eq));  // open: gt, lt
  Multiplexer #(.width(32)) multiplexer_1 (
    .in0(\程序计数器_q ), .in1(32'h3000), .out(PC), .sel(comparator_1_eq));  // open: en
  // Probe on PC
endmodule

module IM (
  input  [31:0] A,
  output [31:0] RD
);

  wire [31:0] subtractor_1_out;

  // Probe on A
  Subtractor #(.width(32)) subtractor_1 (.a(A), .b(32'h3000), .out(subtractor_1_out));  // open: bin, bout
  // Probe on subtractor_1_out
  ROM #(.addrWidth(5), .dataWidth(32)) rom_1 (.addr(subtractor_1_out[6:2]), .data(RD));  // open: sel

  // Notes on the sheet:
  //   contents of rom_1 (hex, n*v repeats v):
  //   35080001 35290001 110afffd 1109fffc
endmodule

module DM (
  input  [31:0] A,
  input  [31:0] WD,
  input  WE,
  input  clk,
  input  reset,
  output [31:0] RD
);

  RAM #(.addrWidth(5), .dataWidth(32), .bus("separate")) ram_1 (
    .addr(A[6:2]), .din(WD), .data(RD), .str(WE), .clk(clk), .clr(reset));  // open: sel, ld
endmodule

module SPLITTER (
  input  [31:0] I,
  output [15:0] Imm_15_0,
  output [4:0] Rd_15_11,
  output [4:0] Rt_20_16,
  output [4:0] Rs_25_21,
  output [5:0] Op_31_26,
  output [5:0] Func_5_0,
  output [4:0] Shamt_10_6,
  output [25:0] Imm26_25_0
);


  assign Func_5_0 = I[5:0];
  assign Imm26_25_0 = I[25:0];
  assign Imm_15_0 = I[15:0];
  assign Op_31_26 = I[31:26];
  assign Rd_15_11 = I[15:11];
  assign Rs_25_21 = I[25:21];
  assign Rt_20_16 = I[20:16];
  assign Shamt_10_6 = I[10:6];
endmodule

module EXT (
  input  [15:0] I,
  input  [2:0] EXTop,
  output [31:0] O
);

  wire [31:0] bit_extender_1_out, bit_extender_2_out;

  assign bit_extender_1_out = {{16{1'b0}}, I};  // Bit_Extender bit_extender_1
  assign bit_extender_2_out = {{16{I[15]}}, I};  // Bit_Extender bit_extender_2
  Multiplexer #(.select(3), .width(32)) multiplexer_1 (
    .in0(bit_extender_1_out), .in1(bit_extender_2_out), .in2({I, {16{1'b0}}}), .out(O), .sel(EXTop));  // open: in3, in4, in5, in6, in7, en
endmodule

module ALU (
  input  [31:0] A,
  input  [4:0] shamt,
  input  [31:0] B,
  input  [3:0] ALUOp,
  output Zero,
  output [31:0] Result
);

  wire [31:0] A_B, A_B_t, A_B_t_t, A_B_t_t_t, sll;

  assign A_B = A & B;  // AND_Gate and_1, 32 bits wide
  assign A_B_t_t_t = A | B;  // OR_Gate or_1, 32 bits wide
  Adder #(.width(32)) adder_1 (.a(A), .b(B), .out(A_B_t));  // open: cin, cout
  Subtractor #(.width(32)) subtractor_1 (.a(A), .b(B), .out(A_B_t_t));  // open: bin, bout
  Shifter #(.width(32)) shifter_1 (.in(B), .\dist (shamt), .out(sll));
  Multiplexer #(.select(4), .width(32)) multiplexer_1 (
    .in0(A_B), .in1(A_B_t_t_t), .in2(A_B_t), .in3(A_B_t_t), .in4(sll), .out(Result), .sel(ALUOp));  // open: in5, in6, in7, in8, in9, in10, in11, in12, in13, in14, in15, en
  Comparator #(.width(32)) comparator_1 (.a({32{1'b0}}), .b(Result), .eq(Zero));  // open: gt, lt
endmodule

module NPC (
  input  [31:0] PC,
  input  [25:0] Imm26,
  input  Zero,
  input  [31:0] RA,
  input  [2:0] NPCOp,
  output [31:0] PC4,
  output [31:0] NPC
);

  wire [15:0] shifter_1_out;
  wire [31:0] adder_2_out, beq, bit_extender_1_out;

  Multiplexer #(.select(3), .width(32)) multiplexer_1 (
    .in0(PC4), .in1(beq), .in2({PC[31:28], Imm26, 2'b00}), .in3(RA), .out(NPC), .sel(NPCOp));  // open: in4, in5, in6, in7, en
  Adder #(.width(32)) adder_1 (.a(PC), .b(32'h4), .out(PC4));  // open: cin, cout
  Shifter #(.width(16)) shifter_1 (.in(Imm26[15:0]), .\dist (4'b0010), .out(shifter_1_out));
  assign bit_extender_1_out = {{16{shifter_1_out[15]}}, shifter_1_out};  // Bit_Extender bit_extender_1
  Adder #(.width(32)) adder_2 (.a(bit_extender_1_out), .b(PC4), .out(adder_2_out));  // open: cin, cout
  Multiplexer #(.width(32)) multiplexer_2 (.in0(PC4), .in1(adder_2_out), .out(beq), .sel(Zero));  // open: en

  // Other names for the same wires on the sheet: jal[31:2] = {PC[31:28], Imm26}
endmodule

module Control (
  input  [5:0] Op,
  input  [5:0] Func,
  output [2:0] RegDstSel,
  output [2:0] ALUSrcSel,
  output [2:0] toRegSel,
  output RegWrite,
  output MemWrite,
  output [2:0] NPCOp,
  output [3:0] ALUOp,
  output [2:0] ExtOp,
  output [2:0] SSel,
  output [2:0] LSel
);

  wire addu, beq, j, jal, jalr, jr, lb, lh, lui, lw, not_1_out, not_2_out, not_3_out, not_4_out, not_5_out,
       not_6_out, not_7_out, not_8_out, not_9_out, not_10_out, not_11_out, not_12_out, ori, R, sb, sh, sll,
       subu, sw;

  not not_1 (not_1_out, Op[5]);
  not not_2 (not_2_out, Op[4]);
  not not_3 (not_3_out, Op[3]);
  buf or_1 (RegDstSel[2], 1'b0);  // OR_Gate
  not not_4 (not_4_out, Op[2]);
  not not_5 (not_5_out, Op[1]);
  buf or_2 (RegDstSel[1], jal);  // OR_Gate
  not not_6 (not_6_out, Op[0]);
  or or_3 (RegDstSel[0], addu, subu, jalr, sll);
  buf or_4 (ALUSrcSel[2], 1'b0);  // OR_Gate
  and u_R (R, not_1_out, not_2_out, not_3_out, not_4_out, not_5_out, not_6_out);
  and u_lw (lw, Op[5], not_2_out, not_3_out, not_4_out, Op[1], Op[0]);
  and u_sw (sw, Op[5], not_2_out, Op[3], not_4_out, Op[1], Op[0]);
  and u_beq (beq, not_1_out, not_2_out, not_3_out, Op[2], not_5_out, not_6_out);
  and u_lui (lui, not_1_out, not_2_out, Op[3], Op[2], Op[1], Op[0]);
  and u_ori (ori, not_1_out, not_2_out, Op[3], Op[2], not_5_out, Op[0]);
  and u_j (j, not_1_out, not_2_out, not_3_out, not_4_out, Op[1], not_6_out);
  and u_jal (jal, not_1_out, not_2_out, not_3_out, not_4_out, Op[1], Op[0]);
  and u_lh (lh, Op[5], not_2_out, not_3_out, not_4_out, not_5_out, Op[0]);
  and u_lb (lb, Op[5], not_2_out, not_3_out, not_4_out, not_5_out, not_6_out);
  and u_sh (sh, Op[5], not_2_out, Op[3], not_4_out, not_5_out, Op[0]);
  and u_sb (sb, Op[5], not_2_out, Op[3], not_4_out, not_5_out, not_6_out);
  buf or_5 (ALUSrcSel[1], 1'b0);  // OR_Gate
  not not_7 (not_7_out, Func[5]);
  or or_6 (ALUSrcSel[0], lw, sw, ori, lh, lb, sh, sb);
  not not_8 (not_8_out, Func[4]);
  buf or_7 (toRegSel[2], 1'b0);  // OR_Gate
  not not_9 (not_9_out, Func[3]);
  or or_8 (toRegSel[1], lui, jal, jalr);
  not not_10 (not_10_out, Func[1]);
  not not_11 (not_11_out, Func[2]);
  or or_9 (toRegSel[0], lw, jal, jalr, lh, lb);
  not not_12 (not_12_out, Func[0]);
  or or_10 (RegWrite, addu, subu, lw, lui, ori, jal, jalr, lh, lb, sll);
  and u_addu (addu, Func[5], not_8_out, not_9_out, not_11_out, not_10_out, not_12_out, R);
  and u_subu (subu, Func[5], not_8_out, not_9_out, not_11_out, Func[1], not_12_out, R);
  and u_jr (jr, not_7_out, not_8_out, Func[3], not_11_out, not_10_out, not_12_out, R);
  and u_jalr (jalr, not_7_out, not_8_out, Func[3], not_11_out, not_10_out, Func[0], R);
  and u_sll (sll, not_7_out, not_8_out, not_9_out, not_11_out, not_10_out, not_12_out, R);
  or or_11 (MemWrite, sw, sh, sb);
  buf or_12 (NPCOp[2], 1'b0);  // OR_Gate
  or or_13 (NPCOp[1], j, jal, jr, jalr);
  or or_14 (NPCOp[0], beq, jr, jalr);
  buf or_15 (ALUOp[3], 1'b0);  // OR_Gate
  buf or_16 (ALUOp[2], sll);  // OR_Gate
  or or_17 (ALUOp[1], sb, addu, subu, lw, sw, beq, lh, lb, sh);
  or or_18 (ALUOp[0], subu, beq, ori);
  buf or_19 (ExtOp[2], 1'b0);  // OR_Gate
  buf or_20 (ExtOp[1], lui);  // OR_Gate
  or or_21 (ExtOp[0], lw, sw, lh, lb, sh, sb);
  buf or_22 (SSel[2], 1'b0);  // OR_Gate
  buf or_23 (SSel[1], sb);  // OR_Gate
  buf or_24 (SSel[0], sh);  // OR_Gate
  buf or_25 (LSel[2], 1'b0);  // OR_Gate
  buf or_26 (LSel[1], lb);  // OR_Gate
  buf or_27 (LSel[0], lh);  // OR_Gate

  // Other names for the same wires on the sheet: F0 = Func[0]; F1 = Func[1]; F2 = Func[2]; F3 = Func[3]; F4 = Func[4];
  //   F5 = Func[5]
endmodule

module DM2 (
  input  [31:0] A,
  input  WE,
  input  clk,
  input  reset,
  input  [31:0] WD,
  input  [2:0] LSel,
  input  [2:0] SSel,
  output [31:0] RD
);

  wire decoder_1_out0, decoder_1_out1, decoder_1_out2, decoder_1_out3;
  wire [7:0] D_7_0, D_23_16, multiplexer_2_out, multiplexer_3_out, multiplexer_4_out, multiplexer_5_out,
       multiplexer_8_out;
  wire [15:0] multiplexer_7_out;
  wire [15:8] D_15_0, D_31_16;
  wire [31:0] bit_extender_1_out, bit_extender_2_out, multiplexer_1_out, multiplexer_6_out;

  // Probe on WD
  Decoder #(.select(2)) decoder_1 (
    .out0(decoder_1_out0), .out1(decoder_1_out1), .out2(decoder_1_out2), .out3(decoder_1_out3), .sel(A[1:0]));  // open: en
  Multiplexer #(.width(32)) multiplexer_1 (
    .in0({D_31_16, D_23_16, WD[15:0]}), .in1({WD[15:0], D_15_0, D_7_0}), .out(multiplexer_1_out), .sel(A[1]));  // open: en
  Multiplexer #(.width(8)) multiplexer_2 (
    .in0(D_7_0), .in1(WD[7:0]), .out(multiplexer_2_out), .sel(decoder_1_out0));  // open: en
  Multiplexer #(.width(8)) multiplexer_3 (
    .in0(D_15_0), .in1(WD[7:0]), .out(multiplexer_3_out), .sel(decoder_1_out1));  // open: en
  Multiplexer #(.width(8)) multiplexer_4 (
    .in0(D_23_16), .in1(WD[7:0]), .out(multiplexer_4_out), .sel(decoder_1_out2));  // open: en
  Multiplexer #(.width(8)) multiplexer_5 (
    .in0(D_31_16), .in1(WD[7:0]), .out(multiplexer_5_out), .sel(decoder_1_out3));  // open: en
  Multiplexer #(.select(3), .width(32)) multiplexer_6 (
    .in0(WD), .in1(multiplexer_1_out),
    .in2({multiplexer_5_out, multiplexer_4_out, multiplexer_3_out, multiplexer_2_out}),
    .out(multiplexer_6_out), .sel(SSel));  // open: in3, in4, in5, in6, in7, en
  // Probe on multiplexer_6_out
  RAM #(.addrWidth(5), .dataWidth(32), .bus("separate")) ram_1 (
    .addr(A[6:2]), .din(multiplexer_6_out), .data({D_31_16, D_23_16, D_15_0, D_7_0}), .str(WE), .clk(clk),
    .clr(reset));  // open: sel, ld
  Multiplexer #(.width(16)) multiplexer_7 (
    .in0({D_15_0, D_7_0}), .in1({D_31_16, D_23_16}), .out(multiplexer_7_out), .sel(A[1]));  // open: en
  Multiplexer #(.select(2), .width(8)) multiplexer_8 (
    .in0(D_7_0), .in1(D_15_0), .in2(D_23_16), .in3(D_31_16), .out(multiplexer_8_out), .sel(A[1:0]));  // open: en
  assign bit_extender_1_out = {{16{multiplexer_7_out[15]}}, multiplexer_7_out};  // Bit_Extender bit_extender_1
  assign bit_extender_2_out = {{24{multiplexer_8_out[7]}}, multiplexer_8_out};  // Bit_Extender bit_extender_2
  Multiplexer #(.select(3), .width(32)) multiplexer_9 (
    .in0({D_31_16, D_23_16, D_15_0, D_7_0}), .in1(bit_extender_1_out), .in2(bit_extender_2_out), .out(RD),
    .sel(LSel));  // open: in3, in4, in5, in6, in7, en

  // Other names for the same wires on the sheet: WD_7_0[7:0] = WD[7:0]; WD_15_0[15:0] = WD[15:0]; D_15_0[7:0] = D_7_0;
  //   D_15_8[7:0] = D_15_0; D_31_16[7:0] = D_23_16; D_31_24[7:0] = D_31_16; A_1_0[1:0] = A[1:0]; A_1 = A[1];
  //   A_6_2[4:0] = A[6:2]
endmodule
